# Fritzing sketch Milestone1_4_3 (saved by Fritzing 0.9.3b)
breadboards: 2

parts:
  Raspberry_Pi_1 = Raspberry Pi 3 [part_number=RPI-3-V1.2]
  R4 = Photocell (LDR) [package=THT]
  R5 = Resistor [tolerance=±5% resistance=220 package=THT]

nets:
  N1: Raspberry_Pi_1.3v3, R4.pin_1
  N2: Raspberry_Pi_1.GPIO27, R4.pin_0, R5.Pin_1
