# Fritzing sketch Milestone1 (saved by Fritzing 0.9.3b)
breadboards: 1

parts:
  Raspberry_Pi_1 = Raspberry Pi 3 [part_number=RPI-3-V1.2]
  Bauteil1 = Arduino Uno (Rev3)
  LED1 = LED - 5mm [color="Red (633nm)" package="5 mm [THT]"]
  R1 = Resistor [tolerance=±5% resistance=220 package=THT]
  R2 = Photocell (LDR) [package=THT]
  R3 = Resistor [tolerance=±5% resistance=220 package=THT]

nets:
  N1: Raspberry_Pi_1.GPIO26, LED1.anode, R1.Pin_0
  N2: Raspberry_Pi_1.GND, R1.Pin_1
  N3: Bauteil1.A0, R2.pin_1, R3.Pin_0
  N4: Bauteil1.3V3, R3.Pin_1
  N5: Bauteil1.GND, R2.pin_0
